// Logisim project testing.circ as structural Verilog: 1 circuit, main circuit main
module main (
  input  in_1,
  input  in_2
);

  wire square_led_1_p1, square_led_2_p1, square_led_3_p1;

  // Square_AND_gate square_and_gate_1: pin names not known; wires that end beside it: in_1
  // Square_LED square_led_1: pin names not known; wires that end beside it: square_led_1_p1, square_led_1_p1
  // Square_OR_gate square_or_gate_1: pin names not known; wires that end beside it: in_2, in_1
  // Square_LED square_led_2: pin names not known; wires that end beside it: square_led_2_p1, square_led_2_p1
  // Square_XOR_gate square_xor_gate_1: pin names not known; wires that end beside it: in_2, in_1, in_2
  // Square_LED square_led_3: pin names not known; wires that end beside it: square_led_3_p1, square_led_3_p1
endmodule
